# Fritzing sketch buttonthing (saved by Fritzing 0.9.4)
breadboards: 1

parts:
  Part1 = Adafruit HUZZAH ESP8266 [part_number="Adafruit #2471"]
  S1 = Pushbutton [package="[THT]"]
  S2 = Pushbutton [package="[THT]"]
  S3 = Pushbutton [package="[THT]"]
  LED1 = LED - 5mm [color="Red (633nm)" package="5 mm [THT]"]
  LED2 = LED - 5mm [color="Red (633nm)" package="5 mm [THT]"]
  R1 = Resistor [tolerance=±5% resistance=220 package=THT]
  R2 = Resistor [tolerance=±5% resistance=220 package=THT]
  X1 = USB Connectors [package=usb-microb]
  S4 = Pushbutton [package="[THT]"]

nets (from the schematic view):
  N1: Part1.GND, S1.Pin_1, S1.Pin_2, S3.Pin_1, S3.Pin_2, S3.Pin_3, S3.Pin_4, R1.Pin_0, R2.Pin_0
  N2: Part1.GPIO16, LED2.anode
  N3: Part1.GPIO13, LED1.anode
  N4: Part1.VBAT, X1.VBUS
  N5: Part1.GPIO2, S1.Pin_3, S1.Pin_4
  N6: S2.Pin_1, S2.Pin_2
  N7: S2.Pin_3, S2.Pin_4
  N8: LED1.cathode, R1.Pin_1
  N9: LED2.cathode, R2.Pin_1
  N10: S4.Pin_1, S4.Pin_2
  N11: S4.Pin_3, S4.Pin_4

custom parts:
  Adafruit HUZZAH ESP8266: Add Internet to your next project with an adorable, bite-sized WiFi microcontroller, at a price you like! The ESP8266 processor from Espressif is an 80 MHz microcontroller with a full WiFi front-end (both as client and access point) and TCP/IP stack with DNS support as well. While this chip has been very popular, its also been very difficult to use. Most of the low cost modules are not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
